# Fritzing sketch Smart-Pets-Feeder (saved by Fritzing 0.9.4)

parts:
  R1 = Resistor [tolerance=±5% resistance=220 package=THT]
  Cycle_Counter = Round Pushbutton
  WeMos_D1_Mini1 = WeMos D1 Mini
  WeMos_D1_Mini_Relay_Shield1 = WeMos D1 Mini Relay Shield
  Power = LED - 5mm [color="Red (633nm)" package="5 mm [THT]"]
  Led_Engine = LED - 5mm [color="Green (555nm)" package="5 mm [THT]"]
  R2ù = Resistor [tolerance=±5% resistance=220 package=THT]
  Power_5V = Power Jack [package=power_jack_pth]
  M1 = Stepper Motor - Bipolar
  Cycle_Counter1 = Round Pushbutton

nets:
  5V: R1.Pin_0, WeMos_D1_Mini1.5V, WeMos_D1_Mini_Relay_Shield1.5V, WeMos_D1_Mini_Relay_Shield1.COM, Power_5V.PWR
  N1: R1.Pin_1, Power.anode
  N2: Cycle_Counter.leg0, WeMos_D1_Mini1.D5
  N3: Cycle_Counter.leg1, WeMos_D1_Mini1.G, WeMos_D1_Mini_Relay_Shield1.G, Power.cathode, Led_Engine.cathode, Power_5V.GNDBREAK, M1.D, Cycle_Counter1.leg1
  N4: WeMos_D1_Mini1.D1, WeMos_D1_Mini_Relay_Shield1.D1
  N5: WeMos_D1_Mini1.D6, Cycle_Counter1.leg0
  N6: WeMos_D1_Mini1.D7, R2ù.Pin_0
  N7: WeMos_D1_Mini_Relay_Shield1.NO, M1.B
  N8: Led_Engine.anode, R2ù.Pin_1

notes:
  Tank level sensor
  By RedFoxy Darrest
  https://me.redfoxy.it
